# Fritzing sketch SprinklerController (saved by Fritzing 1.0.4)
circuit board: 11.9989cm x 5.70076cm
breadboards: 1

parts:
  A2 = Lilygo TTGO T8 ESP32
  A3 = GC9A01 round lcd
  J3 = male pin header, 3 pins [form="♂ (male)"]

nets:
  N1: A2.Pin_14, A3.Pin_2
  N2: A2.Pin_15, A3.Pin_6
  N3: A2.Pin_23, A2.Pin_24
  N4: A2.Pin_25, A2.Pin_26, A2.Pin_28
  N5: A2.Pin_29, A2.Pin_30, A3.Pin_1
  N6: A2.Pin_32, A3.Pin_3
  N7: A2.Pin_34, A3.Pin_4
  N8: A2.Pin_35, A3.Pin_5
  N9: A2.Pin_41, A3.Pin_7
  N10: J3.pin2, J3.pin3

custom parts:
  Lilygo TTGO T8 ESP32: LILYGO® TTGO T8 ESP32-S2 V1.1 WIFI Wireless Module Type-c Connector TF Card Slot Development Board.
  GC9A01 round lcd: IPS TFT display round 1.28″ 240×240 GC9A01 controller.
