# Fritzing sketch Sprinkler_Controller_2-newpart (saved by Fritzing 1.0.4)
circuit board: 8.01128cm x 6.74658cm
breadboards: 1

parts:
  J1 = female pin header, 3 pins [form="♀ (female)"]
  A3 = Lilygo TTGO T8 ESP32
  A4 = GC9A01 round lcd

nets:
  N1: J1.pin1, A3.Pin_41, A4.Pin_7
  N2: J1.pin2, A3.Pin_33
  N3: J1.pin3, A3.Pin_15, A4.Pin_6
  N4: A3.Pin_14, A4.Pin_2
  N5: A3.Pin_29, A3.Pin_30, A4.Pin_1
  N6: A3.Pin_32, A4.Pin_3
  N7: A3.Pin_34, A4.Pin_5
  N8: A3.Pin_35, A4.Pin_4

custom parts:
  Lilygo TTGO T8 ESP32: LILYGO® TTGO T8 ESP32-S2 V1.1 WIFI Wireless Module Type-c Connector TF Card Slot Development Board.
  GC9A01 round lcd: IPS TFT display round 1.28″ 240×240 GC9A01 controller. Mar 2025 fix pcb pin with fill #ffffff instead of none. Casuses problem in etchable pcb images (pad with no hole.)
