# Fritzing sketch Sprinkler_Controller_8a_fill (saved by Fritzing 1.0.4)
circuit board: 8.5cm x 6.75cm
breadboards: 1

parts:
  Mosfet_or_Relay = female pin header, 3 pins [form="♀ (female)"]
  TFT_Display = GC9A01 round lcd
  5v-GND_power = female pin header, 2 pins [form="♀ (female)"]
  TTGO_V8_1_7_1 = Lilygo TTGO T8 ESP32

nets:
  N1: Mosfet_or_Relay.pin1, TFT_Display.Pin_7, TTGO_V8_1_7_1.Pin_41
  N2: Mosfet_or_Relay.pin2, TTGO_V8_1_7_1.Pin_33
  N3: Mosfet_or_Relay.pin3, TFT_Display.Pin_6, TTGO_V8_1_7_1.Pin_15
  N4: TFT_Display.Pin_1, TTGO_V8_1_7_1.Pin_29, TTGO_V8_1_7_1.Pin_30
  N5: TFT_Display.Pin_2, TTGO_V8_1_7_1.Pin_12
  N6: TFT_Display.Pin_3, TTGO_V8_1_7_1.Pin_36
  N7: TFT_Display.Pin_4, TTGO_V8_1_7_1.Pin_35
  N8: TFT_Display.Pin_5, TTGO_V8_1_7_1.Pin_34
  N9: 5v-GND_power.pin1, TTGO_V8_1_7_1.Pin_31
  N10: 5v-GND_power.pin2, TTGO_V8_1_7_1.Pin_28

notes:
  Sprinkler Controller
  +
  -
  S

custom parts:
  GC9A01 round lcd: IPS TFT display round 1.28″ 240×240 GC9A01 controller. Mar 2025 fix pcb pin with fill #ffffff instead of none. Casuses problem in etchable pcb images (pad with no hole.)
  Lilygo TTGO T8 ESP32: LILYGO® TTGO T8 ESP32-S2 V1.1 WIFI Wireless Module Type-c Connector TF Card Slot Development Board.
